# Fritzing sketch Sketch (saved by Fritzing 0.8.7b)
breadboards: 1

parts:
  Part1 = Arduino Uno (Rev3)
  Relay = KY-019 5V Relay Module [package="Breakout board"]
  BAT1 = Battery Holders [package=battery-aaa]
  VALVE1 = Plastic Solenoid Valve
  MOTOR1 = 28BYJ-48 Stepper Motor
  X1 = X113647 Stepper Driver Board [part_number=X113647 package=board]
  Part2 = Bluetooth HC-06  # not connected
  R2 = Photocell (LDR) [package=THT]  # not connected

nets:
  N1: Part1.D9_PWM, Relay.-
  N2: Part1.D10_PWM/SS, X1.IN4
  N3: Part1.D11_PWM/MOSI, X1.IN3
  N4: Part1.D12/MISO, X1.IN2
  N5: Part1.D13/SCK, X1.IN1
  N6: Part1.5V, Relay.+, X1.+V
  GND: Part1.GND, Relay.S, X1.GND
  N7: Relay.NC, BAT1.-
  N8: Relay.NO, VALVE1.no_name_yet#2
  N9: BAT1.+, VALVE1.no_name_yet#1
  N10: MOTOR1.BLUE, X1.BLUE
  N11: MOTOR1.PINK, X1.PINK
  N12: MOTOR1.RED, X1.YELLOW
  N13: MOTOR1.ORANGE, X1.ORANGE
  N14: MOTOR1.YELLOW, X1.RED

custom parts:
  KY-019 5V Relay Module: KY-019 5V Relay module, used to control AC circuits. (Special thanks to vanepp for fixing the PCB holes and other errors)
  28BYJ-48 Stepper Motor: 28BYJ-48 gear-reduction stepper motor (small)
  X113647 Stepper Driver Board: A common stepper motor driver board based on ULN2003APG darlington array
